# Fritzing sketch soft_gripper_board_layout (saved by Fritzing 0.9.3b)
breadboards: 1

parts:
  Part2 = Arduino Uno (Rev3)
  J5 = Camdenboss CTB0158-8 [part_number=CTB0158-8 package=THT]
  J6 = Camdenboss CTB0158-7 [part_number=CTB0158-7 package=THT]
  R5 = Resistor [tolerance=±5% resistance=10k package="0603 [SMD]"]
  R6 = Resistor [tolerance=±5% resistance=10k package="0603 [SMD]"]
  R7 = Resistor [tolerance=±5% resistance=10k package="0603 [SMD]"]
  R8 = Resistor [tolerance=±5% resistance=10k package="0603 [SMD]"]
  J7 = Camdenboss CTB0158-10 [part_number=CTB0158-10 package=THT]
  L1 = Solenoid
  L2 = Solenoid
  J8 = Camdenboss CTB0158-3 [part_number=CTB0158-3 package=THT]
  J9 = Camdenboss CTB0158-3 [part_number=CTB0158-3 package=THT]
  J10 = Camdenboss CTB0158-3 [part_number=CTB0158-3 package=THT]
  J11 = Camdenboss CTB0158-3 [part_number=CTB0158-3 package=THT]
  L3 = Solenoid
  L4 = Solenoid
  J12 = Camdenboss CTB0158-2 [part_number=CTB0158-2 package=THT]
  J13 = Basic Force Sensing Resistor (FSR) [package=THT]
  J14 = Basic Force Sensing Resistor (FSR) [package=THT]
  J15 = Basic Force Sensing Resistor (FSR) [package=THT]
  J16 = Basic Force Sensing Resistor (FSR) [package=THT]

nets:
  N1: Part2.A0, J6.pin5, J6.terminal_4, R5.Pin_1, J14.pin_0
  N2: Part2.A1, J6.pin4, J6.terminal_3, R6.Pin_1, J13.pin_0
  N3: Part2.A2, J6.pin3, J6.terminal_2, R7.Pin_1, J16.pin_0
  N4: Part2.A3, J6.terminal_1, R8.Pin_1, J15.pin_0
  N5: Part2.D8, J5.terminal_5
  N6: Part2.D9_PWM, J5.terminal_6
  N7: Part2.D10_PWM/SS, J5.terminal_7
  N8: Part2.D11_PWM/MOSI, J5.terminal_8
  N9: Part2.D4, J7.terminal_3
  N10: Part2.D5_PWM, J7.terminal_4
  N11: Part2.D6_PWM, J7.terminal_5
  N12: Part2.D7, J7.terminal_6
  N13: Part2.5V, J6.terminal_7, J7.terminal_1, J13.pin_1, J14.pin_1, J15.pin_1, J16.pin_1
  N14: Part2.GND, R5.Pin_0, R6.Pin_0, R7.Pin_0, R8.Pin_0, J7.terminal_2
  N15: L1.pin1, L2.pin1, L3.pin1, L4.pin1, J12.terminal_1
  N16: L1.pin2, J8.terminal_3
  N17: L2.pin2, J9.terminal_3
  N18: J8.terminal_2, J9.terminal_2, J10.terminal_2, J11.terminal_2, J12.terminal_2
  N19: J10.terminal_3, L3.pin2
  N20: J11.terminal_3, L4.pin2

notes:
  optocoupler
  screw terminals
  relay board
  abb 24v / gnd
  pneumatic solenoids
  fingers fsrs
